// Logisim project 16bit.circ as structural Verilog: 11 circuits, main circuit ALU
module main (
  input  [31:0] plus_2
);

  wire bcd_to_7_segment_decoder_2_p1, bcd_to_7_segment_decoder_3_p1, bcd_to_7_segment_decoder_4_p2,
       binary_to_bcd_converter_1_p2, controlunit_1_ain, controlunit_1_alureg_in, controlunit_1_alureg_out,
       controlunit_1_aout, controlunit_1_bin, controlunit_1_bout, controlunit_1_cin, controlunit_1_cout,
       controlunit_1_dar_in, controlunit_1_din, controlunit_1_dout, controlunit_1_ein, controlunit_1_eout,
       controlunit_1_fin, controlunit_1_flag_in, controlunit_1_fout, controlunit_1_gin, controlunit_1_gout,
       controlunit_1_hin, controlunit_1_hout, controlunit_1_iin, controlunit_1_inp, controlunit_1_iout,
       controlunit_1_ir_in, controlunit_1_jin, controlunit_1_jout, controlunit_1_kin, controlunit_1_kout,
       controlunit_1_lin, controlunit_1_lout, controlunit_1_mar_in, controlunit_1_mem_read,
       controlunit_1_mem_write, controlunit_1_min, controlunit_1_mout, controlunit_1_nin, controlunit_1_nout,
       controlunit_1_oin, controlunit_1_oout, controlunit_1_outp, controlunit_1_qin, controlunit_1_qout,
       controlunit_1_tmp_in, decoder_1_out0, decoder_1_out1, decoder_1_out2, decoder_1_out3, decoder_1_out4,
       decoder_1_out5, decoder_1_out6, decoder_1_out7, decoder_1_out8, decoder_1_out9, decoder_1_out10,
       decoder_1_out11, decoder_1_out12, decoder_1_out13, decoder_1_out14, decoder_1_out15, decoder_2_out0,
       decoder_2_out1, decoder_2_out2, decoder_2_out3, decoder_2_out4, decoder_2_out5, decoder_2_out6,
       decoder_2_out7, decoder_2_out8, decoder_2_out9, decoder_2_out10, decoder_2_out11, decoder_2_out12,
       decoder_2_out13, decoder_2_out14, decoder_2_out15, ticking;
  wire [2:0] alu_1_flags, controlunit_1_alu_op, flags_reg_1_data_out;
  wire [3:0] dar_1_data_out;
  wire [6:0] keyboard_1_data;
  wire [12:0] register_1_q;
  wire [31:0] alu_1_result, alureg_1_data_out, ir_1_data_out, mar_reg_1_data_out, rom_1_data,
       tmp_reg_1_data_out;

  ALU alu_1 (
    .ALU_OP(controlunit_1_alu_op), .TMP(tmp_reg_1_data_out), .ACC(alureg_1_data_out), .Result(alu_1_result),
    .FLAGS(alu_1_flags));
  ALUReg alureg_1 (
    .WRITE(controlunit_1_alureg_in), .READ(controlunit_1_alureg_out), .DATA(alu_1_result), .CLOCK(ticking),
    .DATA_OUT(alureg_1_data_out));
  TMP_Reg tmp_reg_1 (
    .WRITE(controlunit_1_tmp_in), .CLOCK(ticking), .DATA(alureg_1_data_out), .DATA_OUT(tmp_reg_1_data_out));
  Clock clock_1 (.out(ticking));
  FLAGS_Reg flags_reg_1 (
    .WRITE(controlunit_1_flag_in), .CLOCK(ticking), .DATA(alu_1_flags), .DATA_OUT(flags_reg_1_data_out));
  // Probe on alureg_1_data_out
  General_purpose_Reg general_purpose_reg_1 (
    .WRITE(controlunit_1_ain), .CLOCK(ticking), .READ(controlunit_1_aout), .DATA(alureg_1_data_out),
    .DATA_OUT(alureg_1_data_out));
  ControlUnit controlunit_1 (
    .Instruction(ir_1_data_out), .FLAGS(flags_reg_1_data_out), .CLOCK(ticking),
    .PCtoBus_in(alureg_1_data_out), .Ain(controlunit_1_ain), .BIn(controlunit_1_bin),
    .CIn(controlunit_1_cin), .DIn(controlunit_1_din), .EIn(controlunit_1_ein), .FIn(controlunit_1_fin),
    .GIn(controlunit_1_gin), .Flag_in(controlunit_1_flag_in), .HIn(controlunit_1_hin),
    .IIn(controlunit_1_iin), .JIn(controlunit_1_jin), .KIn(controlunit_1_kin), .LIn(controlunit_1_lin),
    .Immediate(alureg_1_data_out), .MIn(controlunit_1_min), .NIn(controlunit_1_nin), .OIn(controlunit_1_oin),
    .QIn(controlunit_1_qin), .AOut(controlunit_1_aout), .BOut(controlunit_1_bout), .COut(controlunit_1_cout),
    .DOut(controlunit_1_dout), .EOut(controlunit_1_eout), .FOut(controlunit_1_fout),
    .GOut(controlunit_1_gout), .HOut(controlunit_1_hout), .IOut(controlunit_1_iout),
    .JOut(controlunit_1_jout), .KOut(controlunit_1_kout), .LOut(controlunit_1_lout),
    .MOut(controlunit_1_mout), .NOut(controlunit_1_nout), .OOut(controlunit_1_oout),
    .QOut(controlunit_1_qout), .ALU_OP(controlunit_1_alu_op), .ALUReg_in(controlunit_1_alureg_in),
    .ALUReg_out(controlunit_1_alureg_out), .INP(controlunit_1_inp), .OUTP(controlunit_1_outp),
    .DAR_in(controlunit_1_dar_in), .MAR_in(controlunit_1_mar_in), .TMP_in(controlunit_1_tmp_in),
    .IR_in(controlunit_1_ir_in), .MEM_read(controlunit_1_mem_read), .MEM_write(controlunit_1_mem_write),
    .PCtoBus_out(alureg_1_data_out));  // open: in_4, SP_dec, SP_inc
  Keyboard keyboard_1 (.clk(ticking), .re(decoder_2_out5), .data(keyboard_1_data));  // open: clr, avail
  General_purpose_Reg general_purpose_reg_2 (
    .WRITE(controlunit_1_bin), .CLOCK(ticking), .READ(controlunit_1_bout), .DATA(alureg_1_data_out),
    .DATA_OUT(alureg_1_data_out));
  General_purpose_Reg general_purpose_reg_3 (
    .WRITE(controlunit_1_cin), .CLOCK(ticking), .READ(controlunit_1_cout), .DATA(alureg_1_data_out),
    .DATA_OUT(alureg_1_data_out));
  General_purpose_Reg general_purpose_reg_4 (
    .WRITE(controlunit_1_din), .CLOCK(ticking), .READ(controlunit_1_dout), .DATA(alureg_1_data_out),
    .DATA_OUT(alureg_1_data_out));
  // Probe on alureg_1_data_out
  assign alureg_1_data_out = decoder_2_out5 ? plus_2 : 32'bz;  // Controlled_Buffer controlled_buffer_1
  General_purpose_Reg general_purpose_reg_5 (
    .WRITE(controlunit_1_ein), .CLOCK(ticking), .READ(controlunit_1_eout), .DATA(alureg_1_data_out),
    .DATA_OUT(alureg_1_data_out));
  General_purpose_Reg general_purpose_reg_6 (
    .WRITE(controlunit_1_fin), .CLOCK(ticking), .READ(controlunit_1_fout), .DATA(alureg_1_data_out),
    .DATA_OUT(alureg_1_data_out));
  General_purpose_Reg general_purpose_reg_7 (
    .WRITE(controlunit_1_gin), .CLOCK(ticking), .READ(controlunit_1_gout), .DATA(alureg_1_data_out),
    .DATA_OUT(alureg_1_data_out));
  General_purpose_Reg general_purpose_reg_8 (
    .WRITE(controlunit_1_hin), .CLOCK(ticking), .READ(controlunit_1_hout), .DATA(alureg_1_data_out),
    .DATA_OUT(alureg_1_data_out));
  General_purpose_Reg general_purpose_reg_9 (
    .WRITE(controlunit_1_iin), .CLOCK(ticking), .READ(controlunit_1_iout), .DATA(alureg_1_data_out),
    .DATA_OUT(alureg_1_data_out));
  IR ir_1 (.DATA(alureg_1_data_out), .WRITE(controlunit_1_ir_in), .CLOCK(ticking), .DATA_OUT(ir_1_data_out));
  General_purpose_Reg general_purpose_reg_10 (
    .WRITE(controlunit_1_lin), .CLOCK(ticking), .READ(controlunit_1_lout), .DATA(alureg_1_data_out),
    .DATA_OUT(alureg_1_data_out));
  General_purpose_Reg general_purpose_reg_11 (
    .WRITE(controlunit_1_jin), .CLOCK(ticking), .READ(controlunit_1_jout), .DATA(alureg_1_data_out),
    .DATA_OUT(alureg_1_data_out));
  General_purpose_Reg general_purpose_reg_12 (
    .WRITE(controlunit_1_kin), .CLOCK(ticking), .READ(controlunit_1_kout), .DATA(alureg_1_data_out),
    .DATA_OUT(alureg_1_data_out));
  DAR dar_1 (.CLOCK(ticking), .WRITE(controlunit_1_dar_in), .DATA(alureg_1_data_out), .DATA_OUT(dar_1_data_out));
  Decoder #(.select(4)) decoder_1 (
    .out0(decoder_1_out0), .out1(decoder_1_out1), .out2(decoder_1_out2), .out3(decoder_1_out3),
    .out4(decoder_1_out4), .out5(decoder_1_out5), .out6(decoder_1_out6), .out7(decoder_1_out7),
    .out8(decoder_1_out8), .out9(decoder_1_out9), .out10(decoder_1_out10), .out11(decoder_1_out11),
    .out12(decoder_1_out12), .out13(decoder_1_out13), .out14(decoder_1_out14), .out15(decoder_1_out15),
    .sel(dar_1_data_out), .en(controlunit_1_outp));
  Register #(.width(13)) register_1 (
    .D(alureg_1_data_out[12:0]), .en(decoder_1_out0), .clk(ticking), .Q(register_1_q));  // open: clr
  General_purpose_Reg general_purpose_reg_13 (
    .WRITE(controlunit_1_min), .CLOCK(ticking), .READ(controlunit_1_mout), .DATA(alureg_1_data_out),
    .DATA_OUT(alureg_1_data_out));
  General_purpose_Reg general_purpose_reg_14 (
    .WRITE(controlunit_1_nin), .CLOCK(ticking), .READ(controlunit_1_nout), .DATA(alureg_1_data_out),
    .DATA_OUT(alureg_1_data_out));
  General_purpose_Reg general_purpose_reg_15 (
    .WRITE(controlunit_1_oin), .CLOCK(ticking), .READ(controlunit_1_oout), .DATA(alureg_1_data_out),
    .DATA_OUT(alureg_1_data_out));
  General_purpose_Reg general_purpose_reg_16 (
    .WRITE(controlunit_1_qin), .CLOCK(ticking), .READ(controlunit_1_qout), .DATA(alureg_1_data_out),
    .DATA_OUT(alureg_1_data_out));
  Decoder #(.select(4)) decoder_2 (
    .out0(decoder_2_out0), .out1(decoder_2_out1), .out2(decoder_2_out2), .out3(decoder_2_out3),
    .out4(decoder_2_out4), .out5(decoder_2_out5), .out6(decoder_2_out6), .out7(decoder_2_out7),
    .out8(decoder_2_out8), .out9(decoder_2_out9), .out10(decoder_2_out10), .out11(decoder_2_out11),
    .out12(decoder_2_out12), .out13(decoder_2_out13), .out14(decoder_2_out14), .out15(decoder_2_out15),
    .sel(dar_1_data_out), .en(controlunit_1_inp));
  MAR_Reg mar_reg_1 (
    .WRITE(controlunit_1_mar_in), .CLOCK(ticking), .READ(1'b1), .DATA(alureg_1_data_out),
    .DATA_OUT(mar_reg_1_data_out));
  General_purpose_Reg general_purpose_reg_17 (.DATA_OUT(alureg_1_data_out));  // open: WRITE, CLOCK, READ, DATA
  _7_Segment_Display u_7_segment_display_1 ();  // open: g, f, a, b, e, d, c, dp
  _7_Segment_Display u_7_segment_display_2 ();  // open: g, f, a, b, e, d, c, dp
  // BCD_to_7_Segment_decoder bcd_to_7_segment_decoder_1: pin names not known; wires that end beside it: alureg_1_data_out
  // BCD_to_7_Segment_decoder bcd_to_7_segment_decoder_2: pin names not known; wires that end beside it: bcd_to_7_segment_decoder_2_p1
  // Binary_to_BCD_converter #(.binvalue(13)) binary_to_bcd_converter_1: pin names not known; wires that end beside it: register_1_q, binary_to_bcd_converter_1_p2, binary_to_bcd_converter_1_p2, bcd_to_7_segment_decoder_2_p1
  _7_Segment_Display u_7_segment_display_3 ();  // open: g, f, a, b, e, d, c, dp
  // BCD_to_7_Segment_decoder bcd_to_7_segment_decoder_3: pin names not known; wires that end beside it: bcd_to_7_segment_decoder_3_p1, bcd_to_7_segment_decoder_3_p1
  _7_Segment_Display u_7_segment_display_4 ();  // open: g, f, a, b, e, d, c, dp
  // BCD_to_7_Segment_decoder bcd_to_7_segment_decoder_4: pin names not known; wires that end beside it: controlunit_1_mem_write, bcd_to_7_segment_decoder_4_p2, bcd_to_7_segment_decoder_4_p2
  ROM #(.addrWidth(16), .dataWidth(32)) rom_1 (.addr(mar_reg_1_data_out[15:0]), .data(rom_1_data));
  assign alureg_1_data_out = controlunit_1_mem_read ? rom_1_data : 32'bz;  // Controlled_Buffer controlled_buffer_2

  // Notes on the sheet:
  //   Data Address Regiser
  //   SPregister
  //   To RAM
  //   To RAM
  //   contents of rom_1 (hex, n*v repeats v):
  //   d000005 3d0c0000 c000001 c400001 c800001 d00000f 39100000 14400000 10840000 10080000 d000000
  //   40100000 34ce0000 d000005 39000000
endmodule

module ALU (
  input  [31:0] ACC,
  input  [31:0] TMP,
  input  [2:0] ALU_OP,
  output [31:0] Result,
  output [2:0] FLAGS
);

  wire adder_1_cout, adder_2_cout, decoder_1_out0, decoder_1_out1, decoder_1_out2, decoder_1_out3,
       decoder_1_out4, decoder_1_out5, decoder_1_out6, decoder_1_out7, subtractor_1_bout, subtractor_2_bout;
  wire [31:0] adder_1_out, adder_2_out, and_1_out, not_1_out, or_1_out, subtractor_1_out, subtractor_2_out,
       xor_1_out;

  Decoder #(.select(3)) decoder_1 (
    .out0(decoder_1_out0), .out1(decoder_1_out1), .out2(decoder_1_out2), .out3(decoder_1_out3),
    .out4(decoder_1_out4), .out5(decoder_1_out5), .out6(decoder_1_out6), .out7(decoder_1_out7), .sel(ALU_OP));  // open: en
  assign Result = decoder_1_out0 ? adder_1_out : 32'bz;  // Controlled_Buffer controlled_buffer_1
  Adder #(.width(32)) adder_1 (.a(ACC), .b(TMP), .out(adder_1_out), .cout(adder_1_cout));  // open: cin
  assign FLAGS[1] = decoder_1_out0 ? adder_1_cout : 1'bz;  // Controlled_Buffer controlled_buffer_2
  assign Result = decoder_1_out1 ? subtractor_1_out : 32'bz;  // Controlled_Buffer controlled_buffer_3
  Subtractor #(.width(32)) subtractor_1 (
    .a(ACC), .b(TMP), .out(subtractor_1_out), .bout(subtractor_1_bout));  // open: bin
  assign FLAGS[1] = decoder_1_out1 ? subtractor_1_bout : 1'bz;  // Controlled_Buffer controlled_buffer_4
  assign and_1_out = ACC & TMP;  // AND_Gate and_1, 32 bits wide
  assign Result = decoder_1_out2 ? and_1_out : 32'bz;  // Controlled_Buffer controlled_buffer_5
  assign or_1_out = ACC | TMP;  // OR_Gate or_1, 32 bits wide
  assign Result = decoder_1_out3 ? or_1_out : 32'bz;  // Controlled_Buffer controlled_buffer_6
  assign xor_1_out = ACC ^ TMP;  // XOR_Gate xor_1, 32 bits wide
  assign Result = decoder_1_out4 ? xor_1_out : 32'bz;  // Controlled_Buffer controlled_buffer_7
  assign not_1_out = ~ACC;  // NOT_Gate not_1, 32 bits wide
  assign Result = decoder_1_out5 ? not_1_out : 32'bz;  // Controlled_Buffer controlled_buffer_8
  assign Result = decoder_1_out6 ? adder_2_out : 32'bz;  // Controlled_Buffer controlled_buffer_9
  Adder #(.width(32)) adder_2 (.a(ACC), .b(32'h1), .out(adder_2_out), .cout(adder_2_cout));  // open: cin
  assign FLAGS[1] = decoder_1_out6 ? adder_2_cout : 1'bz;  // Controlled_Buffer controlled_buffer_10
  assign Result = decoder_1_out7 ? subtractor_2_out : 32'bz;  // Controlled_Buffer controlled_buffer_11
  Subtractor #(.width(32)) subtractor_2 (
    .a(ACC), .b(32'h1), .out(subtractor_2_out), .bout(subtractor_2_bout));  // open: bin
  assign FLAGS[1] = decoder_1_out7 ? subtractor_2_bout : 1'bz;  // Controlled_Buffer controlled_buffer_12
  BitSelector #(.width(32)) bitselector_1 (.in(Result), .out(FLAGS[0]), .sel({5{1'b1}}));
  Comparator #(.width(32)) comparator_1 (.a(Result), .b({32{1'b0}}), .eq(FLAGS[2]));  // open: gt, lt

  // Notes on the sheet:
  //   Negative
  //   Carry
  //   Zero
endmodule

module FLAGS_Reg (
  input  [2:0] DATA,
  input  WRITE,
  input  CLOCK,
  output [2:0] DATA_OUT
);

  Register #(.width(3)) register_1 (.D(DATA), .en(WRITE), .clk(CLOCK), .Q(DATA_OUT));  // open: clr
endmodule

module ALUReg (
  input  [31:0] DATA,
  input  WRITE,
  input  CLOCK,
  input  READ,
  output [31:0] DATA_OUT
);

  wire [31:0] register_1_q;

  Register #(.width(32)) register_1 (.D(DATA), .en(WRITE), .clk(CLOCK), .Q(register_1_q));  // open: clr
  assign DATA_OUT = READ ? register_1_q : 32'bz;  // Controlled_Buffer controlled_buffer_1
endmodule

module TMP_Reg (
  input  [31:0] DATA,
  input  WRITE,
  input  CLOCK,
  output [31:0] DATA_OUT
);

  Register #(.width(32)) register_1 (.D(DATA), .en(WRITE), .clk(CLOCK), .Q(DATA_OUT));  // open: clr
endmodule

module General_purpose_Reg (
  input  [31:0] DATA,
  input  WRITE,
  input  CLOCK,
  input  READ,
  output [31:0] DATA_OUT
);

  wire [31:0] register_1_q;

  Register #(.width(32)) register_1 (.D(DATA), .en(WRITE), .clk(CLOCK), .Q(register_1_q));  // open: clr
  assign DATA_OUT = READ ? register_1_q : 32'bz;  // Controlled_Buffer controlled_buffer_1
endmodule

module MAR_Reg (
  input  [31:0] DATA,
  input  WRITE,
  input  CLOCK,
  input  READ,
  output [31:0] DATA_OUT
);

  wire [31:0] register_1_q;

  Register #(.width(32)) register_1 (.D(DATA), .en(WRITE), .clk(CLOCK), .Q(register_1_q));  // open: clr
  assign DATA_OUT = READ ? register_1_q : 32'bz;  // Controlled_Buffer controlled_buffer_1
endmodule

module IR (
  input  [31:0] DATA,
  input  WRITE,
  input  CLOCK,
  output [31:0] DATA_OUT
);

  Register #(.width(32)) register_1 (.D(DATA), .en(WRITE), .clk(CLOCK), .Q(DATA_OUT));  // open: clr
endmodule

module ControlUnit (
  input  [2:0] FLAGS,
  input  [31:0] PCtoBus_in,
  input  CLOCK,
  input  [23:0] in_4,
  input  [31:0] Instruction,
  output AOut,
  output BOut,
  output COut,
  output DOut,
  output EOut,
  output FOut,
  output GOut,
  output HOut,
  output IOut,
  output JOut,
  output KOut,
  output LOut,
  output MOut,
  output NOut,
  output OOut,
  output QOut,
  output Ain,
  output BIn,
  output CIn,
  output DIn,
  output EIn,
  output FIn,
  output GIn,
  output HIn,
  output IIn,
  output JIn,
  output KIn,
  output LIn,
  output MIn,
  output NIn,
  output OIn,
  output QIn,
  output [31:0] PCtoBus_out,
  output SP_dec,
  output SP_inc,
  output IR_in,
  output MEM_read,
  output MEM_write,
  output MAR_in,
  output TMP_in,
  output [2:0] ALU_OP,
  output ALUReg_in,
  output ALUReg_out,
  output INP,
  output OUTP,
  output DAR_in,
  output [31:0] Immediate,
  output Flag_in
);

  wire and_1_out, and_2_out, and_3_out, and_4_out, and_5_out, and_6_out, and_7_out, controlled_buffer_1_out,
       decoder_1_out0, decoder_1_out1, decoder_1_out2, decoder_1_out3, decoder_1_out4, decoder_1_out5,
       decoder_1_out6, decoder_1_out7, decoder_1_out8, decoder_1_out9, decoder_1_out10, decoder_1_out11,
       decoder_1_out12, decoder_1_out13, decoder_1_out14, decoder_1_out15, decoder_2_out0, decoder_2_out1,
       decoder_2_out2, decoder_2_out3, decoder_2_out4, decoder_2_out5, decoder_2_out6, decoder_2_out7,
       decoder_2_out8, decoder_2_out9, decoder_2_out10, decoder_2_out11, decoder_2_out12, decoder_2_out13,
       decoder_2_out14, decoder_2_out15, decoder_3_out0, decoder_3_out1, decoder_3_out2, decoder_3_out3,
       decoder_3_out4, decoder_3_out5, decoder_3_out6, decoder_3_out7, decoder_3_out8, decoder_3_out9,
       decoder_3_out10, decoder_3_out11, decoder_3_out12, decoder_3_out13, decoder_3_out14, decoder_3_out15,
       decoder_4_out0, decoder_4_out1, decoder_4_out2, decoder_4_out3, decoder_4_out4, decoder_4_out5,
       decoder_4_out6, decoder_4_out7, decoder_4_out8, decoder_4_out9, decoder_4_out10, decoder_4_out11,
       decoder_4_out12, decoder_4_out13, decoder_4_out14, decoder_4_out15, not_1_out, not_2_out, or_1_out,
       or_2_out;
  wire [2:0] and_10_out, counter_2_q;
  wire [20:6] ControlWord;
  wire [23:0] rom_1_data, rom_2_data;
  wire [31:0] counter_1_q;

  assign controlled_buffer_1_out = and_7_out ? ControlWord[12] : 1'bz;  // Controlled_Buffer controlled_buffer_1
  and and_1 (and_1_out, ControlWord[12], FLAGS[1]);
  assign controlled_buffer_1_out = and_6_out ? and_1_out : 1'bz;  // Controlled_Buffer controlled_buffer_2
  and and_2 (and_2_out, FLAGS[0], ControlWord[12]);
  assign controlled_buffer_1_out = and_5_out ? and_2_out : 1'bz;  // Controlled_Buffer controlled_buffer_3
  and and_3 (and_3_out, FLAGS[2], ControlWord[12]);
  assign controlled_buffer_1_out = and_4_out ? and_3_out : 1'bz;  // Controlled_Buffer controlled_buffer_4
  assign {DAR_in, OUTP, INP, ControlWord[20], SP_inc, SP_dec, ControlWord[17], IR_in, MEM_write, MEM_read, ControlWord[13:11], MAR_in, ControlWord[9:6], TMP_in, ALU_OP, ALUReg_out, ALUReg_in} = or_1_out ? rom_1_data : 24'bz;  // Controlled_Buffer controlled_buffer_5
  ROM #(.addrWidth(3), .dataWidth(24)) rom_1 (.addr(and_10_out), .data(rom_1_data));
  Counter #(.max('hffffffff), .width(32)) counter_1 (
    .load(controlled_buffer_1_out), .up(1'b1), .count(ControlWord[13]), .clk(CLOCK), .D(PCtoBus_in),
    .Q(counter_1_q));  // open: clr, carry
  and and_4 (and_4_out, ~Instruction[21], Instruction[20]);  // AND_Gate
  and and_5 (and_5_out, Instruction[21], ~Instruction[20]);  // AND_Gate
  and and_6 (and_6_out, Instruction[21], Instruction[20]);
  and and_7 (and_7_out, ~Instruction[21], ~Instruction[20]);  // AND_Gate
  or or_1 (or_1_out, and_10_out[0], and_10_out[2], and_10_out[1]);
  assign PCtoBus_out = ControlWord[11] ? counter_1_q : 32'bz;  // Controlled_Buffer controlled_buffer_6
  Counter #(.max('h7), .width(3)) counter_2 (
    .up(1'b1), .count(1'b1), .clk(not_1_out), .Q(counter_2_q));  // open: clr, load, D, carry
  not not_1 (not_1_out, CLOCK);
  and and_8 (and_10_out[1], counter_2_q[0], ~counter_2_q[1], ~counter_2_q[2]);  // AND_Gate
  and and_9 (and_10_out[2], ~counter_2_q[0], counter_2_q[1], ~counter_2_q[2]);  // AND_Gate
  and and_10 (and_10_out[0], ~counter_2_q[0], ~counter_2_q[1], ~counter_2_q[2]);  // AND_Gate
  or or_2 (or_2_out, and_10_out[0], and_10_out[2], and_10_out[1]);
  not not_2 (not_2_out, or_2_out);
  ROM #(.addrWidth(9), .dataWidth(24)) rom_2 (.addr({Instruction[31:26], counter_2_q}), .data(rom_2_data));
  Decoder #(.select(4)) decoder_1 (
    .out0(decoder_1_out0), .out1(decoder_1_out1), .out2(decoder_1_out2), .out3(decoder_1_out3),
    .out4(decoder_1_out4), .out5(decoder_1_out5), .out6(decoder_1_out6), .out7(decoder_1_out7),
    .out8(decoder_1_out8), .out9(decoder_1_out9), .out10(decoder_1_out10), .out11(decoder_1_out11),
    .out12(decoder_1_out12), .out13(decoder_1_out13), .out14(decoder_1_out14), .out15(decoder_1_out15),
    .sel(Instruction[21:18]), .en(ControlWord[6]));
  // Probe on {Instruction[31:26], counter_2_q}
  or or_3 (Ain, decoder_1_out0, decoder_2_out0);
  or or_4 (BIn, decoder_1_out1, decoder_2_out1);
  or or_5 (CIn, decoder_1_out2, decoder_2_out2);
  or or_6 (DIn, decoder_1_out3, decoder_2_out3);
  assign {DAR_in, OUTP, INP, ControlWord[20], SP_inc, SP_dec, ControlWord[17], IR_in, MEM_write, MEM_read, ControlWord[13:11], MAR_in, ControlWord[9:6], TMP_in, ALU_OP, ALUReg_out, ALUReg_in} = not_2_out ? rom_2_data : 24'bz;  // Controlled_Buffer controlled_buffer_7
  or or_7 (EIn, decoder_1_out4, decoder_2_out4);
  or or_8 (FIn, decoder_1_out5, decoder_2_out5);
  and and_11 (Flag_in, Instruction[17], ControlWord[17]);
  or or_9 (GIn, decoder_1_out6, decoder_2_out6);
  or or_10 (HIn, decoder_1_out7, decoder_2_out7);
  or or_11 (IIn, decoder_1_out8, decoder_2_out8);
  or or_12 (JIn, decoder_1_out9, decoder_2_out9);
  or or_13 (KIn, decoder_1_out10, decoder_2_out10);
  or or_14 (LIn, decoder_1_out11, decoder_2_out11);
  Decoder #(.select(4)) decoder_2 (
    .out0(decoder_2_out0), .out1(decoder_2_out1), .out2(decoder_2_out2), .out3(decoder_2_out3),
    .out4(decoder_2_out4), .out5(decoder_2_out5), .out6(decoder_2_out6), .out7(decoder_2_out7),
    .out8(decoder_2_out8), .out9(decoder_2_out9), .out10(decoder_2_out10), .out11(decoder_2_out11),
    .out12(decoder_2_out12), .out13(decoder_2_out13), .out14(decoder_2_out14), .out15(decoder_2_out15),
    .sel(Instruction[25:22]), .en(ControlWord[20]));
  assign Immediate = ControlWord[8] ? {{10{1'b0}}, Instruction[21:0]} : 32'bz;  // Controlled_Buffer controlled_buffer_8
  or or_15 (MIn, decoder_1_out12, decoder_2_out12);
  or or_16 (NIn, decoder_1_out13, decoder_2_out13);
  or or_17 (OIn, decoder_1_out14, decoder_2_out14);
  or or_18 (QIn, decoder_1_out15, decoder_2_out15);
  or or_19 (AOut, decoder_3_out0, decoder_4_out0);
  Decoder #(.select(4)) decoder_3 (
    .out0(decoder_3_out0), .out1(decoder_3_out1), .out2(decoder_3_out2), .out3(decoder_3_out3),
    .out4(decoder_3_out4), .out5(decoder_3_out5), .out6(decoder_3_out6), .out7(decoder_3_out7),
    .out8(decoder_3_out8), .out9(decoder_3_out9), .out10(decoder_3_out10), .out11(decoder_3_out11),
    .out12(decoder_3_out12), .out13(decoder_3_out13), .out14(decoder_3_out14), .out15(decoder_3_out15),
    .sel(Instruction[21:18]), .en(ControlWord[9]));
  or or_20 (BOut, decoder_3_out1, decoder_4_out1);
  or or_21 (COut, decoder_3_out2, decoder_4_out2);
  or or_22 (DOut, decoder_3_out3, decoder_4_out3);
  or or_23 (EOut, decoder_3_out4, decoder_4_out4);
  or or_24 (FOut, decoder_3_out5, decoder_4_out5);
  or or_25 (GOut, decoder_3_out6, decoder_4_out6);
  or or_26 (HOut, decoder_3_out7, decoder_4_out7);
  or or_27 (IOut, decoder_3_out8, decoder_4_out8);
  or or_28 (JOut, decoder_3_out9, decoder_4_out9);
  or or_29 (KOut, decoder_3_out10, decoder_4_out10);
  or or_30 (LOut, decoder_3_out11, decoder_4_out11);
  or or_31 (MOut, decoder_3_out12, decoder_4_out12);
  Decoder #(.select(4)) decoder_4 (
    .out0(decoder_4_out0), .out1(decoder_4_out1), .out2(decoder_4_out2), .out3(decoder_4_out3),
    .out4(decoder_4_out4), .out5(decoder_4_out5), .out6(decoder_4_out6), .out7(decoder_4_out7),
    .out8(decoder_4_out8), .out9(decoder_4_out9), .out10(decoder_4_out10), .out11(decoder_4_out11),
    .out12(decoder_4_out12), .out13(decoder_4_out13), .out14(decoder_4_out14), .out15(decoder_4_out15),
    .sel(Instruction[25:22]), .en(ControlWord[7]));
  or or_32 (NOut, decoder_3_out13, decoder_4_out13);
  or or_33 (OOut, decoder_3_out14, decoder_4_out14);
  or or_34 (QOut, decoder_3_out15, decoder_4_out15);

  // Other names for the same wires on the sheet: JMPmode[1:0] = Instruction[1:0]; Rdst[3:0] = Instruction[21:18];
  //   Conditions_for_ind_jmp[1:0] = Instruction[21:20];
  //   ControlWord (some bits) = {DAR_in, OUTP, INP, SP_inc, SP_dec, IR_in, MEM_write, MEM_read, MAR_in, TMP_in, ALU_OP, ALUReg_out, ALUReg_in};
  //   Conditions[1:0] = Instruction[25:24]; Rsrc[3:0] = Instruction[25:22]; Rdst_in = ControlWord[6];
  //   Rsrc_out = ControlWord[7]; Imm_out = ControlWord[8]; Rdst_out = ControlWord[9]; PC_out = ControlWord[11];
  //   PC_in = ControlWord[12]; PC_inc = ControlWord[13]; Flag_in_t = ControlWord[17]; Rsrc_in = ControlWord[20]

  // Notes on the sheet:
  //   contents of rom_1 (hex, n*v repeats v):
  //   0 c00 14000 0 2000
  //   contents of rom_2 (hex, n*v repeats v):
  //   11*0 480 4040 6*0 600 8080 6*0 100100 7*0 c0 7*0 220 20081 42 5*0 220 20085 42 5*0 220 20084 6*0 220
  //   20089 42 5*0 220 2008d 42 5*0 220 20091 42 6*0 20095 42 6*0 20099 42 6*0 2009d 42 5*0 1080 7*0
  //   800080 200040 6*0 800200 400080 6*0 4200 8000 6*0 1800 4080 4080 8000 4*0 10000 80000
endmodule

module DAR (
  input  [31:0] DATA,
  input  WRITE,
  input  CLOCK,
  output [3:0] DATA_OUT
);

  wire [31:4] register_1_q;

  Register #(.width(32)) register_1 (.D(DATA), .en(WRITE), .clk(CLOCK), .Q({register_1_q, DATA_OUT}));  // open: clr
endmodule

module ToOutput (
  input  [3:0] in_1
);
endmodule
